# Fritzing sketch gateway (saved by Fritzing 0.9.6b)
breadboards: 2

parts:
  U1 = ESP32-38PinWide [part_number=ESP32-38PinWide]
  R1 = Trimmer Potentiometer [maximum_resistance=10kΩ package=THT]
  LED1 = LED - 5mm [color="Red (633nm)" current=0.030 package="5 mm [THT]"]
  LED2 = smd LED [color="Green (565nm)" package="1206 [SMD]"]
  S1 = Pushbutton [package="[SMD]"]
  R2 = Resistor [tolerance=±1% power=0.25W resistance=10k package=THT]
  LCD1 = LCD screen
  R3 = Resistor [tolerance=±1% power=0.25W resistance=10k package=THT]
  R4 = Resistor [tolerance=±1% power=0.25W resistance=10k package=THT]
  S2 = Pushbutton [package="[THT]"]
  S3 = Pushbutton [package="[THT]"]

nets:
  N1: U1.3.3, S1.Pin_3, S1.Pin_4, S2.Pin_3, S2.Pin_4, S3.Pin_3, S3.Pin_4
  N2: U1.GPIO33, LCD1.DB4
  N3: U1.GPIO25, LCD1.DB5
  N4: U1.GPIO26, LCD1.DB6
  N5: U1.GPIO27, LCD1.DB7
  N6: U1.GPIO14, LCD1.E
  N7: U1.GPIO12, LCD1.RS
  GND: U1.GND, R1.leg2, LED1.cathode, LED2.anode, R2.Pin_0, LCD1.VSS, LCD1.R/W, LCD1.LED-, R3.Pin_0, R4.Pin_0
  VIN: U1.VIN, R1.leg1, LCD1.VDD, LCD1.LED+
  N8: U1.GPIO16, LED1.anode
  N9: U1.GPIO17, LED2.cathode
  N10: U1.GPIO21, R3.Pin_1, S2.Pin_1, S2.Pin_2
  N11: U1.GPIO22, S1.Pin_1, S1.Pin_2, R2.Pin_1
  N12: U1.GPIO23, R4.Pin_1, S3.Pin_1, S3.Pin_2
  N13: R1.wiper, LCD1.V0

notes:
  5V
  3,3V
  UP
  DOWN

custom parts:
  ESP32-38PinWide: Generic 38-Pin ESP32 with wide format (only access to one side of pins on a breadboard) based on Stephen Lilley's HiLetgo ESP-WROOM-32 ESP32 ESP-32S Development Board.
