# Fritzing sketch sensor (saved by Fritzing 0.9.6b)
breadboards: 2

parts:
  U1 = ESP32-38PinWide [part_number=ESP32-38PinWide]
  DHT1 = Humidity and Temperature Sensor DHT11
  R3 = Resistor [tolerance=±5% power=0.25 resistance=10k package=THT]
  R4 = PHOTOCELL [package=photocell-kit]
  LED1 = LED - 5mm [color="Red (633nm)" current=0.030 package="5 mm [THT]"]

nets:
  N1: U1.3.3, DHT1.Vcc, R3.Pin_1
  N2: U1.GPIO34, LED1.anode
  N3: U1.GPIO32, R3.Pin_0, R4.P$2
  N4: U1.GPIO11, DHT1.GND_2, R4.P$1, LED1.cathode

custom parts:
  ESP32-38PinWide: Generic 38-Pin ESP32 with wide format (only access to one side of pins on a breadboard) based on Stephen Lilley's HiLetgo ESP-WROOM-32 ESP32 ESP-32S Development Board.
  Humidity and Temperature Sensor DHT11: Digital relative humidity & temperature sensor DHT11
